// Logisim project Regfile.circ as structural Verilog: 1 circuit, main circuit reg
module \reg  (
  input  [1:0] Read_register_1,
  input  [1:0] Read_register_2,
  input  [1:0] write_register,
  input  [15:0] write_data,
  input  RegWrite,
  input  clock,
  output [15:0] Reg_0_Value,
  output [15:0] Reg_1_Value,
  output [15:0] Reg_2_Value,
  output [15:0] Reg_3_Value,
  output [15:0] Read_Data_1,
  output [15:0] Read_Data_2
);

  wire Write_1, Write_2, Write_3, Write_4;

  Register #(.width(16)) register_1 (.D(write_data), .en(Write_1), .Q(Reg_0_Value), .clk(clock));  // open: clr
  Demultiplexer #(.select(2), .enable("false")) demultiplexer_1 (
    .out0(Write_1), .out1(Write_2), .out2(Write_3), .out3(Write_4), .in(RegWrite), .sel(write_register));
  Register #(.width(16)) register_2 (.D(write_data), .en(Write_2), .Q(Reg_1_Value), .clk(clock));  // open: clr
  Register #(.width(16)) register_3 (.D(write_data), .en(Write_3), .Q(Reg_2_Value), .clk(clock));  // open: clr
  Register #(.width(16)) register_4 (.D(write_data), .en(Write_4), .Q(Reg_3_Value), .clk(clock));  // open: clr
  Multiplexer #(.select(2), .width(16)) multiplexer_1 (
    .in0(Reg_0_Value), .in1(Reg_1_Value), .in2(Reg_2_Value), .in3(Reg_3_Value), .out(Read_Data_1),
    .sel(Read_register_1));  // open: en
  Multiplexer #(.select(2), .width(16)) multiplexer_2 (
    .in0(Reg_0_Value), .in1(Reg_1_Value), .in2(Reg_2_Value), .in3(Reg_3_Value), .out(Read_Data_2),
    .sel(Read_register_2));  // open: en

  // Other names for the same wires on the sheet: data[15:0] = write_data; Read_1[1:0] = Read_register_1;
  //   Read_2[1:0] = Read_register_2; Reg_0[15:0] = Reg_0_Value; Reg_1[15:0] = Reg_1_Value; Reg_2[15:0] = Reg_2_Value;
  //   Reg_3[15:0] = Reg_3_Value

  // Notes on the sheet:
  //   These are INPUTS to the circuit
  //   These are INPUTS to the circuit
  //   DO NOT CHANGE THE LOCATIONS OF THE INPUTS/OUTPUTS! IF YOU DO SO, YOU NEED TO MAKE SURE THE PINS ARE AT THE RIGHT PLACE!
  //   These are OUTPUTS to the circuit
  //   Yet again, the clock is not an actual clock, but an input, one that will be driven from a higher circuit
  //   These are OUTPUTS to the circuit
endmodule
