// Logisim project cpu.circ as structural Verilog: 10 circuits, main circuit main
module main (
  input  [15:0] From_Instr_Mem,
  input  clk,
  output [15:0] r0,
  output [15:0] r1,
  output [15:0] r2,
  output [15:0] r3,
  output [15:0] Display_0,
  output [15:0] Display_1,
  output [15:0] To_Instr_Mem,
  output [15:0] Data_Mem_Addr,
  output [15:0] Data_Mem_Data,
  output Data_Mem_Write
);

  wire alu_1_signed_overflow, ALUsrc, AND_2_out, AND_3_out, beq, bne, display, equal, imm_select, jal, jr,
       Jump, lui, MemRead, MemtoReg, nop, not_1_out, RegDst, RegWrite, Reset_out, rtype, select, take_branch,
       \unsigned ;
  wire [1:0] rd, rs, rt, Write_Reg;
  wire [3:0] ALU_switch, ALUOp, opcode;
  wire [5:0] funct;
  wire [7:0] imm;
  wire [11:0] instruction_splitter_1_target_address;
  wire [15:0] adder_2_out, AND_out, ext_imm, multiplexer_1_out, multiplexer_2_out, multiplexer_4_out,
       multiplexer_5_out, multiplexer_6_out, operation_performed_1_output_1, operation_performed_1_output_2,
       OR_out, PC___1, PC_q, read_rs, read_rt, target_address, Write_Data;

  kill_instruction kill_instruction_1 (
    .beq(beq), .equal(equal), .bne(bne), .jr(jr), .jal(jal), .jump(Jump), .take_branch(take_branch), .nop(nop));
  Button Reset (.out(Reset_out));
  not not_1 (not_1_out, Data_Mem_Write);
  Register #(.width(16)) PC (.D(multiplexer_1_out), .Q(PC_q), .clk(clk));  // open: en, clr
  Multiplexer #(.width(16), .enable("false")) multiplexer_1 (
    .in0(From_Instr_Mem), .in1(16'h6), .out(multiplexer_1_out), .sel(nop));
  assign Data_Mem_Data = Data_Mem_Write ? read_rt : 16'bz;  // Controlled_Buffer Controlled_buffer
  RAM #(.addrWidth(16), .dataWidth(16)) ram_1 (
    .addr(Data_Mem_Addr), .data(Data_Mem_Data), .sel(1'b1), .clk(clk), .ld(not_1_out), .clr(Reset_out));
  instruction_splitter instruction_splitter_1 (
    .PC_Input(PC_q), .funct(funct), .immediate(imm), .rd(rd), .rt(rt), .rs(rs), .opcode(opcode),
    .target_address(instruction_splitter_1_target_address));
  assign target_address = {{4{1'b0}}, instruction_splitter_1_target_address};  // Bit_Extender bit_extender_1
  Adder #(.width(16)) adder_1 (.a(To_Instr_Mem), .b(16'h1), .out(PC___1));  // open: cin, cout
  Register #(.width(16)) register_1 (.D(multiplexer_6_out), .Q(To_Instr_Mem), .clk(clk));  // open: en, clr
  extend_immediate u_ext_imm (.imm_in(imm), .imm_extended(ext_imm), .\unsigned (\unsigned ));
  Multiplexer #(.width(16), .enable("false")) multiplexer_2 (
    .in0(Data_Mem_Addr), .in1(Data_Mem_Data), .out(multiplexer_2_out), .sel(MemtoReg));
  write_register write_register (.rt(rt), .rd(rd), .write_register(Write_Reg), .RegDst(RegDst), .jal(jal));
  // main_control main_control_1: pin names not known; wires that end beside it: bne, beq, MemRead, MemtoReg, Data_Mem_Write, Jump, ALUsrc, \unsigned , imm_select, opcode, lui, ALUOp, rtype, RegDst, display, RegWrite, jal, jr
  Multiplexer #(.width(16), .enable("false")) multiplexer_3 (
    .in0(multiplexer_2_out), .in1(To_Instr_Mem), .out(Write_Data), .sel(jal));
  assign AND_out = To_Instr_Mem & 16'hf000;  // AND_Gate AND, 16 bits wide
  funct funct_1 (.switch_output(ALU_switch), .opcode(opcode), .funct_in(funct));
  Multiplexer #(.width(16), .enable("false")) multiplexer_4 (
    .in0(PC___1), .in1(OR_out), .out(multiplexer_4_out), .sel(Jump));
  assign OR_out = AND_out | target_address;  // OR_Gate OR, 16 bits wide
  Hex_Digit_Display hex_digit_display_1 (.value(Display_0[15:12]));  // open: dp
  Hex_Digit_Display hex_digit_display_2 (.value(Display_0[11:8]));  // open: dp
  and AND_2 (AND_2_out, ~select, display);  // AND_Gate
  Multiplexer #(.width(16), .enable("false")) multiplexer_5 (
    .in0(multiplexer_4_out), .in1(read_rs), .out(multiplexer_5_out), .sel(jr));
  Adder #(.width(16)) adder_2 (.a(To_Instr_Mem), .b(ext_imm), .out(adder_2_out));  // open: cin, cout
  Hex_Digit_Display hex_digit_display_3 (.value(Display_0[7:4]));  // open: dp
  Hex_Digit_Display hex_digit_display_4 (.value(Display_0[3:0]));  // open: dp
  Register #(.width(16)) register_2 (.D(read_rs), .en(AND_2_out), .Q(Display_0), .clk(clk));  // open: clr
  LED LED (.in(alu_1_signed_overflow));
  operation_performed operation_performed_1 (
    .lui(lui), .rs_in(read_rs), .rt_in(read_rt), .imm_in(ext_imm), .output_1(operation_performed_1_output_1),
    .output_2(operation_performed_1_output_2), .imm_select(ALUsrc));
  alu alu_1 (
    .Switch__S(ALU_switch), .X(operation_performed_1_output_1), .Equal(equal), .RESULT(Data_Mem_Addr),
    .Signed_Overflow(alu_1_signed_overflow), .Y(operation_performed_1_output_2));
  \reg  reg_1 (
    .Read_register_1(rs), .Read_register_2(rt), .write_register(Write_Reg), .write_data(Write_Data),
    .Reg_0_Value(r0), .Reg_1_Value(r1), .Reg_2_Value(r2), .Reg_3_Value(r3), .RegWrite(RegWrite), .clock(clk),
    .Read_Data_1(read_rs), .Read_Data_2(read_rt));
  Multiplexer #(.width(16), .enable("false")) multiplexer_6 (
    .in0(multiplexer_5_out), .in1(adder_2_out), .out(multiplexer_6_out), .sel(take_branch));
  Hex_Digit_Display hex_digit_display_5 (.value(Display_1[15:12]));  // open: dp
  BitSelector #(.width(16)) bitselector_1 (.in(ext_imm), .out(select), .sel(4'b0000));
  Hex_Digit_Display hex_digit_display_6 (.value(Display_1[11:8]));  // open: dp
  Hex_Digit_Display hex_digit_display_7 (.value(Display_1[7:4]));  // open: dp
  Register #(.width(16)) register_3 (.D(read_rs), .en(AND_3_out), .Q(Display_1), .clk(clk));  // open: clr
  and AND_3 (AND_3_out, select, display);
  Hex_Digit_Display hex_digit_display_8 (.value(Display_1[3:0]));  // open: dp

  // Other names for the same wires on the sheet: CurrPC[15:0] = To_Instr_Mem; d0[15:0] = Display_0;
  //   d1[15:0] = Display_1; ins_out[15:0] = Data_Mem_Addr; MemWrite = Data_Mem_Write; RAM[15:0] = Data_Mem_Data

  // Notes on the sheet:
  //   This is the current PC that you need to send as OUTPUT
  //   This is the instruction that you would receive as INPUT
  //   This is a CLK that is an INPUT driven from the harness.
  //   Remember, this circuit is loaded from the harness to be tested!
  //   DATA MEMORY
  //   These are OUTPUTS of the circuit
  //   INSTRUCTION FETCH
  //   INSTRUCTION EXECUTE
  //   DO NOT CHANGE THE LOCATIONS OF THE INPUTS OR OUTPUTS! IF YOU DO SO, YOU NEED TO MAKE SURE THE PINS ARE IN THE RIGHT PLACES!
  //   CONTROL
  //   These are OUTPUTS of the circuit
  //   INSTRUCTION DECODE
  //   DISPLAY
endmodule

// ins split
module instruction_splitter (
  input  [15:0] PC_Input,
  output [5:0] funct,
  output [7:0] immediate,
  output [1:0] rd,
  output [1:0] rt,
  output [1:0] rs,
  output [3:0] opcode,
  output [11:0] target_address
);


  assign funct = PC_Input[5:0];
  assign immediate = PC_Input[7:0];
  assign opcode = PC_Input[15:12];
  assign rd = PC_Input[7:6];
  assign rs = PC_Input[11:10];
  assign rt = PC_Input[9:8];
  assign target_address = PC_Input[11:0];
endmodule

module main_control (
  input  [3:0] opcode,
  output RegDst,
  output display,
  output RegWrite,
  output jal,
  output jr,
  output rtype,
  output lui,
  output [3:0] ALUOp,
  output bne,
  output beq,
  output MemRead,
  output MemtoReg,
  output MemWrite,
  output Jump,
  output ALUSrc,
  output \unsigned ,
  output imm_select
);

  wire addi, andi, beq_t, bne_t, disp, j, jal_t, jr_t, lw, ori, sw;

  opcode_decoder opcode_decoder_1 (
    .R_type(rtype), .jal(jal_t), .j(j), .jr(jr_t), .beq(beq_t), .addi(addi), .andi(andi), .ori(ori),
    .bne(bne_t), .sw(sw), .lui(lui), .lw(lw), .disp(disp), .opcode(opcode));
  control_select control_select_1 (
    .rtype(rtype), .disp(disp), .lui(lui), .ori(ori), .addi(addi), .andi(andi), .jal(jal_t), .j(j),
    .jr(jr_t), .beq(beq_t), .bne(bne_t), .lw(lw), .sw(sw), .RegDst(RegDst), .display(display),
    .RegWrite(RegWrite), .jal_2(jal), .jr_2(jr), .bne_2(bne), .beq_2(beq), .MemRead(MemRead),
    .MemtoReg(MemtoReg), .MemWrite(MemWrite), .Jump(Jump), .ALUSrc(ALUSrc), .\unsigned (\unsigned ),
    .imm_select(imm_select), .ALUOp(ALUOp));
endmodule

// contol select
module control_select (
  input  rtype,
  input  disp,
  input  lui,
  input  ori,
  input  addi,
  input  andi,
  input  jal,
  input  j,
  input  jr,
  input  beq,
  input  bne,
  input  lw,
  input  sw,
  output RegDst,
  output display,
  output RegWrite,
  output jal_2,
  output jr_2,
  output [3:0] ALUOp,
  output bne_2,
  output beq_2,
  output MemRead,
  output MemtoReg,
  output MemWrite,
  output Jump,
  output ALUSrc,
  output \unsigned ,
  output imm_select
);

  or or_1 (RegWrite, rtype, lui, ori, addi, andi, jal, lw);
  or or_2 (Jump, j, jal);
  or or_3 (ALUSrc, sw, lw, andi, addi, ori, lui, disp);
  or or_4 (ALUOp[0], beq, bne, andi);
  or or_5 (\unsigned , lui, ori, disp, andi);
  or or_6 (ALUOp[1], addi, beq, bne, lw, sw);
  or or_7 (imm_select, addi, lui, ori, sw, lw);

  assign ALUOp[3:2] = {1'b0, lui};
  assign beq_2 = beq;
  assign bne_2 = bne;
  assign display = disp;
  assign jal_2 = jal;
  assign jr_2 = jr;
  assign MemRead = lw;
  assign MemtoReg = lw;
  assign MemWrite = sw;
  assign RegDst = rtype;
endmodule

module opcode_decoder (
  input  [3:0] opcode,
  output R_type,
  output jal,
  output j,
  output jr,
  output beq,
  output addi,
  output andi,
  output ori,
  output bne,
  output sw,
  output lui,
  output lw,
  output disp
);

  Decoder #(.select(4), .enable("false")) decoder_1 (
    .out0(R_type), .out1(jal), .out2(j), .out3(jr), .out4(beq), .out5(addi), .out6(andi), .out7(ori),
    .out8(bne), .out9(sw), .out10(lui), .out11(lw), .out12(disp), .sel(opcode));  // open: out13, out14, out15
endmodule

// kill
module kill_instruction (
  input  beq,
  input  equal,
  input  bne,
  input  jr,
  input  jal,
  input  jump,
  output take_branch,
  output nop
);

  wire AND_2_out, AND_out, branch, not_1_out;

  and AND (AND_out, beq, equal);
  not not_1 (not_1_out, equal);
  and AND_2 (AND_2_out, not_1_out, bne);
  or OR (branch, jr, jal, jump);
  or OR_2 (take_branch, AND_out, AND_2_out);
  or OR_3 (nop, AND_out, AND_2_out, branch);
endmodule

module funct (
  input  [5:0] funct_in,
  input  [3:0] opcode,
  output [3:0] switch_output
);

  wire [3:0] bit_extender_1_out;

  Bit_Extender #(.in_width(6), .out_width(4)) bit_extender_1 (.in(funct_in), .out(bit_extender_1_out));
  Multiplexer #(.select(4), .width(4), .enable("false")) multiplexer_1 (
    .in0(bit_extender_1_out), .in5(4'b0000), .in6(4'b0111), .in7(4'b0110), .in9(4'b0000), .in10(4'b0010),
    .in11(4'b0000), .out(switch_output), .sel(opcode));  // open: in1, in2, in3, in4, in8, in12, in13, in14, in15
endmodule

module write_register (
  input  [1:0] rt,
  input  [1:0] rd,
  input  RegDst,
  input  jal,
  output [1:0] write_register
);

  wire [1:0] multiplexer_1_out;

  Multiplexer #(.width(2), .enable("false")) multiplexer_1 (.in0(rt), .in1(rd), .out(multiplexer_1_out), .sel(RegDst));
  Multiplexer #(.width(2), .enable("false")) multiplexer_2 (
    .in0(multiplexer_1_out), .in1(2'b11), .out(write_register), .sel(jal));
endmodule

// op per
module operation_performed (
  input  lui,
  input  [15:0] rs_in,
  input  [15:0] rt_in,
  input  [15:0] imm_in,
  input  imm_select,
  output [15:0] output_1,
  output [15:0] output_2
);

  wire [15:0] multiplexer_2_out;

  Multiplexer #(.width(16), .enable("false")) multiplexer_1 (.in0(rs_in), .in1(imm_in), .out(output_1), .sel(lui));
  Multiplexer #(.width(16), .enable("false")) multiplexer_2 (
    .in0(rt_in), .in1(imm_in), .out(multiplexer_2_out), .sel(imm_select));
  Multiplexer #(.width(16), .enable("false")) multiplexer_3 (
    .in0(multiplexer_2_out), .in1(16'h8), .out(output_2), .sel(lui));
endmodule

module extend_immediate (
  input  [7:0] imm_in,
  input  \unsigned ,
  output [15:0] imm_extended
);

  wire [15:0] bit_extender_1_out, bit_extender_2_out;

  assign bit_extender_1_out = {{8{imm_in[7]}}, imm_in};  // Bit_Extender bit_extender_1
  assign bit_extender_2_out = {{8{1'b0}}, imm_in};  // Bit_Extender bit_extender_2
  Multiplexer #(.width(16), .enable("false")) multiplexer_1 (
    .in0(bit_extender_1_out), .in1(bit_extender_2_out), .out(imm_extended), .sel(\unsigned ));
endmodule
