// Logisim project alu.circ as structural Verilog: 7 circuits, main circuit alu
module alu (
  input  [15:0] X,
  input  [15:0] Y,
  input  [3:0] Switch__S,
  output [15:0] RESULT,
  output Equal,
  output Signed_Overflow
);

  wire AddOverflow_out, Addp8Overflow_out, comparator_1_lt, SubOverflow_out, Subp8Overflow_out;
  wire [15:0] add, addp8, \and , \or , sllv, slt, srav, srlv, sub, subp8;

  assign \and  = X & Y;  // AND_Gate AND, 16 bits wide
  assign \or  = X | Y;  // OR_Gate OR, 16 bits wide
  Comparator #(.width(16)) comparator_1 (.a(X), .b(Y), .lt(comparator_1_lt));  // open: gt, eq
  Shifter #(.width(16)) shifter_1 (.in(X), .\dist (Y[3:0]), .out(sllv));
  Shifter #(.width(16), .shift("lr")) shifter_2 (.in(X), .\dist (Y[3:0]), .out(srlv));
  Shifter #(.width(16), .shift("ar")) shifter_3 (.in(X), .\dist (Y[3:0]), .out(srav));
  Adder #(.width(16)) adder_1 (.a(X), .b(Y), .out(add));  // open: cin, cout
  Subtractor #(.width(16)) subtractor_1 (.a(X), .b(Y), .out(sub));  // open: bin, bout
  Addp8 u_Addp8 (.X(X), .Y(Y), .\output (addp8));
  Subp8 u_Subp8 (.X(X), .Y(Y), .\output (subp8));
  assign slt = {{15{1'b0}}, comparator_1_lt};  // Bit_Extender bit_extender_1
  Multiplexer #(.select(4), .enable("false")) multiplexer_1 (
    .in0(AddOverflow_out), .in1(SubOverflow_out), .in2(Addp8Overflow_out), .in3(Subp8Overflow_out),
    .out(Signed_Overflow), .sel(Switch__S));  // open: in4, in5, in6, in7, in8, in9, in10, in11, in12, in13, in14, in15
  AddOverflow AddOverflow (.X(Y), .Y(X), .out(AddOverflow_out));
  SubOverflow SubOverflow (.X(Y), .Y(X), .out(SubOverflow_out));
  Addp8Overflow Addp8Overflow (.X(Y), .Y(X), .out(Addp8Overflow_out));
  Subp8Overflow Subp8Overflow (.X(Y), .Y(X), .out(Subp8Overflow_out));
  Multiplexer #(.select(4), .width(16), .enable("false")) multiplexer_2 (
    .in0(add), .in1(sub), .in2(sllv), .in3(srlv), .in4(srav), .in5(slt), .in6(\or ), .in7(\and ),
    .in8(addp8), .in9(subp8), .out(RESULT), .sel(Switch__S));  // open: in10, in11, in12, in13, in14, in15
  Comparator #(.width(16)) comparator_2 (.a(X), .b(Y), .eq(Equal));  // open: gt, lt

  // Other names for the same wires on the sheet: S[3:0] = Switch__S

  // Notes on the sheet:
  //   INPUT to your circuit
  //   INPUTS to your circuit
  //   slt
  //   sllv
  //   srlv
  //   srav
  //   add
  //   sub
  //   DON'T CHANGE THE INPUTS AND OUTPUTS! IF YOU DO SO, YOU NEED TO MAKE SURE THE PINS ARE IN THE RIGHT PLACES!
  //   OUTPUTS of your circuit
endmodule

module AddOverflow (
  input  [15:0] X,
  input  [15:0] Y,
  output out
);

  wire AND_2_out, AND_out, not_1_out, not_2_out, not_3_out;
  wire [15:0] adder_1_out;

  Adder #(.width(16)) adder_1 (.a(X), .b(Y), .out(adder_1_out));  // open: cin, cout
  not not_1 (not_1_out, X[15]);
  not not_2 (not_2_out, adder_1_out[15]);
  not not_3 (not_3_out, Y[15]);
  and AND (AND_out, not_1_out, adder_1_out[15], not_3_out);
  and AND_2 (AND_2_out, X[15], not_2_out, Y[15]);
  or OR (out, AND_out, AND_2_out);
endmodule

module SubOverflow (
  input  [15:0] X,
  input  [15:0] Y,
  output out
);

  wire AND_2_out, AND_out, not_1_out, not_2_out, not_3_out;
  wire [15:0] adder_1_out;

  Adder #(.width(16)) adder_1 (.a(X), .b(Y), .out(adder_1_out));  // open: cin, cout
  not not_1 (not_1_out, X[15]);
  not not_2 (not_2_out, adder_1_out[15]);
  not not_3 (not_3_out, Y[15]);
  and AND (AND_out, not_1_out, adder_1_out[15], Y[15]);
  and AND_2 (AND_2_out, X[15], not_2_out, not_3_out);
  or OR (out, AND_out, AND_2_out);
endmodule

module Addp8 (
  input  [15:0] X,
  input  [15:0] Y,
  output [15:0] \output 
);

  wire adder_1_cout;

  Adder adder_1 (.a(X[7:0]), .b(Y[7:0]), .out(\output [7:0]), .cout(adder_1_cout));  // open: cin
  Adder adder_2 (.a(X[15:8]), .b(Y[15:8]), .out(\output [15:8]), .cin(adder_1_cout));  // open: cout
endmodule

module Subp8 (
  input  [15:0] X,
  input  [15:0] Y,
  output [15:0] \output 
);

  wire subtractor_1_bout;

  Subtractor subtractor_1 (.a(X[7:0]), .b(Y[7:0]), .out(\output [7:0]), .bout(subtractor_1_bout));  // open: bin
  Subtractor subtractor_2 (.a(X[15:8]), .b(Y[15:8]), .out(\output [15:8]), .bin(subtractor_1_bout));  // open: bout
endmodule

module Addp8Overflow (
  input  [15:0] X,
  input  [15:0] Y,
  output out
);

  wire AND_2_out, AND_out, not_1_out, not_2_out, not_3_out;
  wire [15:0] addp8_1_output;

  Addp8 addp8_1 (.X(X), .Y(Y), .\output (addp8_1_output));
  not not_1 (not_1_out, X[15]);
  not not_2 (not_2_out, addp8_1_output[15]);
  not not_3 (not_3_out, Y[15]);
  and AND (AND_out, not_1_out, addp8_1_output[15], not_3_out);
  and AND_2 (AND_2_out, X[15], not_2_out, Y[15]);
  or OR (out, AND_out, AND_2_out);
endmodule

module Subp8Overflow (
  input  [15:0] X,
  input  [15:0] Y,
  output out
);

  wire AND_2_out, AND_out, not_1_out, not_2_out, not_3_out;
  wire [15:0] subp8_1_output;

  Subp8 subp8_1 (.X(X), .Y(Y), .\output (subp8_1_output));
  not not_1 (not_1_out, X[15]);
  not not_2 (not_2_out, subp8_1_output[15]);
  not not_3 (not_3_out, Y[15]);
  and AND (AND_out, not_1_out, subp8_1_output[15], Y[15]);
  and AND_2 (AND_2_out, X[15], not_2_out, not_3_out);
  or OR (out, AND_out, AND_2_out);
endmodule
